// Logisim project GCD.circ as structural Verilog: 1 circuit, main circuit main
module main (
  input  [15:0] Number,
  input  [7:0] n,
  input  go,
  output [15:0] GCD,
  output EnterNewNumber
);

  wire clock_1_out, main_1_a, main_1_b, main_1_c, main_1_d, main_1_na, main_2_ldi, main_2_ldn, main_2_ldx,
       main_2_ldy, main_2_si, main_2_ssub1, main_2_ssub2, main_2_sx, main_2_sy;

  Clock clock_1 (.out(clock_1_out));
  datapath_main main_1 (
    .Number(Number), .sy(main_2_sy), .ldy(main_2_ldy), .n_i(n), .ldi(main_2_ldi), .ldn(main_2_ldn),
    .CLK(clock_1_out), .sx(main_2_sx), .ssub1(main_2_ssub1), .si(main_2_si), .ldx(main_2_ldx),
    .ssub2(main_2_ssub2), .GCD(GCD), .c(main_1_c), .d(main_1_d), .b(main_1_b), .na(main_1_na), .a(main_1_a));
  control_unit_main main_2 (
    .na(main_1_na), .CLK(clock_1_out), .b(main_1_b), .c(main_1_c), .d(main_1_d), .go(go),
    .NewNumber(EnterNewNumber), .sx(main_2_sx), .sy(main_2_sy), .si(main_2_si), .ssub1(main_2_ssub1),
    .ssub2(main_2_ssub2), .ldx(main_2_ldx), .a(main_1_a), .ldy(main_2_ldy), .ldn(main_2_ldn), .ldi(main_2_ldi));
endmodule
