// Logisim project control_unit.circ as structural Verilog: 1 circuit, main circuit main
module main (
  input  a,
  input  na,
  input  CLK,
  input  b,
  input  c,
  input  d,
  input  go,
  output sx,
  output sy,
  output si,
  output NewNumber,
  output ssub1,
  output ssub2,
  output ldx,
  output ldy,
  output ldn,
  output ldi
);

  wire and_2_out, and_3_out, and_4_out, and_5_out, and_6_out, decoder_1_out0, decoder_1_out2, decoder_1_out4,
       or_1_out, or_2_out, or_3_out, or_4_out, or_5_out;
  wire [2:0] P0_q;

  D_Flip_Flop P2 (.clk(CLK), .D(or_3_out), .Q(P0_q[2]), .en(1'b1));  // open: Qn, preset, reset
  D_Flip_Flop P1 (.clk(CLK), .D(or_4_out), .Q(P0_q[1]), .en(1'b1));  // open: Qn, preset, reset
  D_Flip_Flop P0 (.clk(CLK), .D(or_5_out), .Q(P0_q[0]), .en(1'b1));  // open: Qn, preset, reset
  and and_1 (NewNumber, decoder_1_out2, a);
  Decoder #(.select(3), .enable("false")) decoder_1 (
    .out0(decoder_1_out0), .out1(ldn), .out2(decoder_1_out2), .out3(si), .out4(decoder_1_out4), .out5(ssub1),
    .out6(ssub2), .sel(P0_q));  // open: out7
  and and_2 (and_2_out, decoder_1_out0, go);
  and and_3 (and_3_out, na, decoder_1_out2);
  and and_4 (and_4_out, decoder_1_out4, or_1_out);
  or or_1 (or_1_out, b, c);
  or or_2 (or_2_out, c, d);
  and and_5 (and_5_out, b, decoder_1_out4);
  or or_3 (or_3_out, and_3_out, si, ssub1, ssub2, and_4_out);
  and and_6 (and_6_out, decoder_1_out4, or_2_out);
  or or_4 (or_4_out, ldn, decoder_1_out2, and_6_out);
  or or_5 (or_5_out, decoder_1_out2, and_5_out, and_2_out);
  or or_6 (ldx, ldn, ssub2);
  or or_7 (ldy, si, ssub1);
  or or_8 (ldi, ldn, si);

  assign sx = ldn;
  assign sy = si;
endmodule
