// Logisim project datapath.circ as structural Verilog: 1 circuit, main circuit main
module main (
  input  ssub1,
  input  sx,
  input  [15:0] Number,
  input  ldx,
  input  sy,
  input  ssub2,
  input  ldy,
  input  [7:0] n_i,
  input  si,
  input  ldi,
  input  ldn,
  input  CLK,
  output [15:0] GCD,
  output c,
  output d,
  output b,
  output na,
  output a
);

  wire comparator_1_eq, comparator_1_gt;
  wire [7:0] adder_1_out, i_q, multiplexer_3_out, n_q;
  wire [15:0] multiplexer_1_out, multiplexer_2_out, multiplexer_4_out, multiplexer_5_out, subtractor_1_out,
       Y_q;

  Multiplexer #(.width(16), .enable("false")) multiplexer_1 (
    .in0(subtractor_1_out), .in1(Number), .out(multiplexer_1_out), .sel(sx));
  Multiplexer #(.width(16), .enable("false")) multiplexer_2 (
    .in0(subtractor_1_out), .in1(Number), .out(multiplexer_2_out), .sel(sy));
  Multiplexer #(.width(8), .enable("false")) multiplexer_3 (
    .in0(8'h1), .in1(adder_1_out), .out(multiplexer_3_out), .sel(si));
  Register #(.width(16)) X (.D(multiplexer_1_out), .en(ldx), .Q(GCD), .clk(CLK));  // open: clr
  Register #(.width(16)) Y (.D(multiplexer_2_out), .en(ldy), .Q(Y_q), .clk(CLK));  // open: clr
  Register i (.D(multiplexer_3_out), .en(ldi), .Q(i_q), .clk(CLK));  // open: clr
  Register n (.D(n_i), .en(ldn), .Q(n_q), .clk(CLK));  // open: clr
  Comparator comparator_1 (.a(i_q), .b(n_q), .gt(comparator_1_gt), .eq(comparator_1_eq), .lt(a));
  Multiplexer #(.width(16), .enable("false")) multiplexer_4 (
    .in0(GCD), .in1(Y_q), .out(multiplexer_4_out), .sel(ssub1));
  Multiplexer #(.width(16), .enable("false")) multiplexer_5 (
    .in0(GCD), .in1(Y_q), .out(multiplexer_5_out), .sel(ssub2));
  Comparator #(.width(16)) comparator_2 (.a(GCD), .b(Y_q), .gt(c), .eq(d), .lt(b));
  Adder adder_1 (.a(i_q), .b(8'h1), .out(adder_1_out));  // open: cin, cout
  or or_1 (na, comparator_1_gt, comparator_1_eq);
  Subtractor #(.width(16)) subtractor_1 (
    .a(multiplexer_4_out), .b(multiplexer_5_out), .out(subtractor_1_out));  // open: bin, bout
endmodule
